# Fritzing sketch EEG Circuit (saved by Fritzing 0.9.1b)
circuit board: 6.88566cm x 5.36311cm
breadboards: 1

parts:
  IC1 = IC, DIP package, 8 pins [chip_label=AD620]
  R1 = Resistor [tolerance=±5% resistance=560 package=THT]
  IC2 = OP482 - Low Power, High Speed JFET Quad Operational Amplifier [part_number=TL084]
  R2 = Resistor [tolerance=±5% resistance=22k package=THT]
  C1 = Ceramic Capacitor [capacitance=220nF package="100 mil [THT, multilayer]"]
  C2 = Electrolytic Capacitor [capacitance=10µF package="100 mil [THT, electrolytic]"]
  R3 = Resistor [tolerance=±5% resistance=220 package=THT]
  R4 = Resistor [tolerance=±5% resistance=12 package=THT]
  C3 = Ceramic Capacitor [capacitance=220nF package="100 mil [THT, multilayer]"]
  C4 = Ceramic Capacitor [capacitance=220nF package="100 mil [THT, multilayer]"]
  C5 = Ceramic Capacitor [capacitance=220nF package="100 mil [THT, multilayer]"]
  R5 = Resistor [tolerance=±5% resistance=220 package=THT]
  R6 = Resistor [tolerance=±5% resistance=180k package=THT]
  R7 = Resistor [tolerance=±5% resistance=180k package=THT]
  R8 = Resistor [tolerance=±5% resistance=180k package=THT]
  C6 = Ceramic Capacitor [capacitance=100nF package="100 mil [THT, multilayer]"]
  C7 = Ceramic Capacitor [capacitance=25nF package="100 mil [THT, multilayer]"]
  C8 = Electrolytic Capacitor [capacitance=1µF package="100 mil [THT, electrolytic]"]
  R9 = Resistor [tolerance=±5% resistance=1M package=THT]
  C9 = Ceramic Capacitor [capacitance=10nF package="100 mil [THT, multilayer]"]
  R10 = Resistor [tolerance=±5% resistance=100 package=THT]
  IC3 = OP482 - Low Power, High Speed JFET Quad Operational Amplifier [part_number=TL084]
  R12 = Trimmer Potentiometer [maximum_resistance=2kΩ package=THT]
  R11 = Resistor [tolerance=±5% resistance=220 package=THT]
  R13 = Resistor [tolerance=±5% resistance=22k package=THT]
  Part1 = Arduino Uno (Rev3)
  C10 = Electrolytic Capacitor [capacitance=10µF package="100 mil [THT, electrolytic]"]
  C11 = Ceramic Capacitor [capacitance=220nF package="100 mil [THT, multilayer]"]
  R14 = Resistor [tolerance=±5% resistance=12 package=THT]
  R15 = Resistor [tolerance=±5% resistance=220 package=THT]

nets:
  N1: IC1.pin1, R1.Pin_0
  0V: IC1.pin4, IC2.V-, IC3.V-, Part1.GND
  GND: IC1.pin5, IC2.+INB, IC2.+INC, R3.Pin_1, C6.0, R9.Pin_0, R12.leg1, R15.Pin_1
  N2: IC1.pin6, R2.Pin_0
  5V: IC1.pin7, IC2.V+, IC3.V+, Part1.5V
  N3: IC1.pin8, R1.Pin_1
  N4: IC2.OUTA, IC2.-INA, R4.Pin_1, C3.0
  N5: IC2.+INA, C2.-, R3.Pin_0
  N6: IC2.-INB, C5.1, R5.Pin_1
  N7: IC2.OUTB, C4.1, R5.Pin_0, R6.Pin_0
  N8: IC2.OUTC, R8.Pin_1, C7.1, C8.+
  N9: IC2.-INC, R7.Pin_1, C7.0
  N10: IC2.+IND, C8.-, R9.Pin_1
  N11: IC2.-IND, C9.0, R10.Pin_1, R11.Pin_0
  N12: IC2.OUTD, C9.1, R10.Pin_0, R13.Pin_0
  N13: R2.Pin_1, C1.0
  N14: C1.1, C2.+, R4.Pin_0
  N15: C3.1, C4.0, C5.0
  N16: R6.Pin_1, R7.Pin_0, R8.Pin_0, C6.1
  N17: IC3.OUTA, IC3.-INA, C10.+, R14.Pin_1
  N18: IC3.+INA, C10.-, R15.Pin_0
  N19: R12.wiper, R11.Pin_1
  N20: R13.Pin_1, Part1.A0, C11.1
  N21: C11.0, R14.Pin_0

notes:
  EEG Circuit 3, By Alexander Pope, 3
